# Fritzing sketch Sketch1 (saved by Fritzing 0.9.3b)
breadboards: 1

parts:
  R1 = Resistor [tolerance=±5% resistance=220 package=THT]
  R2 = PHOTOCELL [package=photocell]
  LED1 = LED - 3mm [color="Red (633nm)" package="3 mm [THT]"]
  Part1 = Photon
  R3 = Resistor [tolerance=±5% resistance=220 package=THT]

nets:
  N1: R1.Pin_0, R2.P$2
  N2: R1.Pin_1, Part1.GND, R3.Pin_1
  N3: R2.P$1, Part1.A0
  N4: LED1.cathode, R3.Pin_0
  N5: LED1.anode, Part1.D0
